# Fritzing sketch sprayDigital copy (saved by Fritzing 0.6.2b)
breadboards: 1

parts:
  XTAL1 = Crystal [frequency="16 Mhz" package=THT]
  ATmega328 = atmega168 [package="DIP28 [THT]"]
  C3 = Ceramic Capacitor [capacitance=22µF voltage=20V package="100 mil [THT, multilayer]"]
  C4 = Ceramic Capacitor [capacitance=22µF voltage=20V package="100 mil [THT, multilayer]"]
  R17 = Resistor [tolerance=±5% resistance=220 package=THT]
  XBee = XBee
  J9 = female pin header, 2 pins [form="♀ (female)"]
  S3 = Pushbutton [package=THT]
  78L33 = Voltage Regulator - 3.3V [package="TO220 [THT]"]
  cor = female pin header, 3 pins [form="♀ (female)"]
  U4 = Voltage Regulator - 5V [package="TO220 [THT]"]
  R18 = Resistor [tolerance=±5% resistance=10k package=THT]
  LED10 = white LED - 5mm [package="5 mm [THT]"]
  C5 = Electrolytic Capacitor [capacitance=10µF voltage=20V package="100 mil [THT, electrolytic]"]
  LED11 = Red LED - 5mm [package="5 mm [THT]"]
  R19 = Resistor [tolerance=±5% resistance=220 package=THT]
  RESET = Pushbutton [package="[THT]"]
  TX = Resistor [tolerance=±5% resistance=100 package=THT]
  R21 = Resistor [tolerance=±5% resistance=3.3k package=THT]
  RX = Resistor [tolerance=±5% resistance=1.8k package=THT]
  R23 = Resistor [tolerance=±5% resistance=470 package=THT]
  LED12 = Red LED - 5mm [package="5 mm [THT]"]
  LED_RGB = female pin header, 4 pins [form="♀ (female)"]
  distancia = female pin header, 3 pins [form="♀ (female)"]
  let/bot = female pin header, 2 pins [form="♀ (female)"]
  J10 = female pin header, 10 pins [form="♀ (female)"]
  J11 = female pin header, 10 pins [form="♀ (female)"]
  RX_2 = Red LED - 5mm [package="5 mm [THT]"]
  TX_2 = green LED - 5mm [package="5 mm [THT]"]
  R24 = Resistor [tolerance=±5% resistance=1k package=THT]
  R25 = Resistor [tolerance=±5% resistance=1k package=THT]

nets:
  N1: XTAL1.pin_0, ATmega328.Pin_10, C4.1
  N2: XTAL1.pin_1, ATmega328.Pin_9, C3.0
  N3: ATmega328.Pin_1, R18.Pin_0, RESET.Pin_1, RESET.Pin_2
  N4: ATmega328.Pin_2, TX.Pin_1
  N5: ATmega328.Pin_3, RX.Pin_1
  N6: ATmega328.Pin_5, LED_RGB.pin4
  N7: ATmega328.Pin_7, ATmega328.Pin_20, ATmega328.Pin_21, cor.pin1, U4.output_voltage, R18.Pin_1, distancia.pin1, let/bot.pin1
  GND: ATmega328.Pin_8, ATmega328.Pin_22, C3.1, C4.0, XBee.GND, J9.pin2, 78L33.GND, cor.pin2, U4.GND, C5.-, LED11.cathode, RESET.Pin_3, RESET.Pin_4, R21.Pin_0, R23.Pin_1, distancia.pin2, J10.pin10, RX_2.cathode, TX_2.cathode
  N8: ATmega328.Pin_11, LED_RGB.pin3
  N9: ATmega328.Pin_12, LED_RGB.pin2
  N10: ATmega328.Pin_18, R17.Pin_1
  N11: ATmega328.Pin_23, cor.pin3
  N12: ATmega328.Pin_24, distancia.pin3
  N13: R17.Pin_0, let/bot.pin2
  N14: XBee.VCC, 78L33.output_voltage, J10.pin1
  N15: XBee.pin2, TX.Pin_0, J10.pin2, R24.Pin_1
  N16: XBee.pin3, R21.Pin_1, RX.Pin_0, J10.pin3, R25.Pin_1
  N17: XBee.pin4, J10.pin4
  N18: XBee.pin5, J10.pin5
  N19: XBee.pin6, LED12.cathode, J10.pin6
  N20: XBee.pin7, J10.pin7
  N21: XBee.pin8, J10.pin8
  N22: XBee.pin9, J10.pin9
  N23: XBee.pin11, J11.pin10
  N24: XBee.pin12, J11.pin9
  N25: XBee.pin13, J11.pin8
  N26: XBee.pin14, J11.pin7
  N27: XBee.pin15, J11.pin6
  N28: XBee.pin16, J11.pin5
  N29: XBee.pin17, J11.pin4
  N30: XBee.pin18, J11.pin3
  N31: XBee.pin19, J11.pin2
  N32: XBee.pin20, J11.pin1
  N33: J9.pin1, 78L33.input_voltage, U4.input_voltage, C5.+, R19.Pin_0, LED_RGB.pin1
  N34: S3.leg1, LED10.anode
  N35: LED11.anode, R19.Pin_1
  N36: R23.Pin_0, LED12.anode
  N37: RX_2.anode, R25.Pin_0
  N38: TX_2.anode, R24.Pin_0

notes:
  VCC GND
  S - +
  S +
