# Fritzing sketch sprayDigital_xbee_shield (saved by Fritzing 0.6.2b)

parts:
  Part1 = Arduino XBee Shield
  J1 = Infrared Proximity Sensor
  R1 = Rotary Potentiometer (Large) [maximum_resistance=100kΩ package=THT]
  LED1 = white LED - 5mm [package="5 mm [THT]"]  # not connected

nets:
  N1: Part1.A0, J1.Vout
  N2: Part1.A1, R1.wiper
  N3: Part1.N$104, R1.leg2
  N4: Part1.N$117, R1.leg1
  N5: Part1.N$128, J1.Vcc
  N6: Part1.N$129, J1.GND
